# Fritzing sketch schematics (saved by Fritzing 0.9.3b)

parts:
  Part1 = Arduino Nano (Rev3.0)
  IR_Receiver = TSOP312.., 314.. [package=THT]
  DOTSTAR_led_strip = DotStar Strip -- White (60/m) [part_number=2240]
  Power2 = Adafruit Micro USB Breakout [part_number="Adafruit #1833"]
  Power1 = Adafruit Micro USB Breakout [part_number="Adafruit #1833"]
  Channel_5 = Adafruit Micro USB Breakout [part_number="Adafruit #1833"]
  Channel_6 = Adafruit Micro USB Breakout [part_number="Adafruit #1833"]
  Channel_7 = Adafruit Micro USB Breakout [part_number="Adafruit #1833"]
  Channel_8 = Adafruit Micro USB Breakout [part_number="Adafruit #1833"]
  Channel_1 = Adafruit Micro USB Breakout [part_number="Adafruit #1833"]
  Channel_4 = Adafruit Micro USB Breakout [part_number="Adafruit #1833"]
  Channel_3 = Adafruit Micro USB Breakout [part_number="Adafruit #1833"]
  Channel_2 = Adafruit Micro USB Breakout [part_number="Adafruit #1833"]
  Spike_absorbtion_capacitor = Capacitor Polarized [package=cpol-radial-1000uf-25v]
  Spike_absorbtion_resistor = Resistor [tolerance=±5% resistance=27 package="0603 [SMD]"]
  Spike_absorbtion_resistor_2 = Resistor [tolerance=±5% resistance=27 package="0603 [SMD]"]
  miscro_usb_plug = USB_MICROB_PLUG [package=micro-b-ra-th]
  IR_recevier_socket = Adafruit Micro USB Breakout [part_number="Adafruit #1833"]
  miscro_usb_plug_2 = USB_MICROB_PLUG [package=micro-b-ra-th]

nets:
  GND: Part1.GND, Power2.GND, Power2.ID, Power1.GND, Power1.ID, Channel_5.GND, Channel_6.GND, Channel_7.GND, Channel_8.GND, Channel_1.GND, Channel_4.GND, Channel_4.ID, Channel_3.GND, Channel_3.ID, Channel_2.GND, Channel_2.ID, Spike_absorbtion_capacitor.-, IR_recevier_socket.GND
  N1: Part1.D4, Channel_1.D+
  N2: Part1.D5, Channel_2.D+
  N3: Part1.D6, Channel_3.D+
  N4: Part1.D7, Channel_4.D+
  N5: Part1.D9, Channel_1.D-, Channel_4.D-, Channel_3.D-, Channel_2.D-
  N6: Part1.D10, Channel_5.D-, Channel_6.D-, Channel_7.D-, Channel_8.D-
  N7: Part1.VIN, Power2.D+, Power2.D-, Power2.VBUS, Power1.VBUS, Channel_5.VBUS, Channel_6.VBUS, Channel_7.VBUS, Channel_8.VBUS, Channel_1.VBUS, Channel_4.VBUS, Channel_3.VBUS, Channel_2.VBUS, Spike_absorbtion_capacitor.+, IR_recevier_socket.VBUS
  N8: Part1.A5, Channel_5.D+
  N9: Part1.A4, Channel_6.D+
  N10: Part1.A3, Channel_7.D+
  N11: Part1.A2, Channel_8.D+
  N12: Part1.A0, IR_recevier_socket.D+
  GND_2: IR_Receiver.GND, miscro_usb_plug_2.GND
  N13: IR_Receiver.Vs, miscro_usb_plug_2.VCC
  N14: IR_Receiver.Data, miscro_usb_plug_2.D+
  +5V: DOTSTAR_led_strip.+5V, miscro_usb_plug.VCC
  N15: DOTSTAR_led_strip.DI, Spike_absorbtion_resistor_2.Pin_0
  GND_3: DOTSTAR_led_strip.GND, miscro_usb_plug.GND
  N16: DOTSTAR_led_strip.CI, Spike_absorbtion_resistor.Pin_0
  N17: Spike_absorbtion_resistor.Pin_1, miscro_usb_plug.D-
  N18: Spike_absorbtion_resistor_2.Pin_1, miscro_usb_plug.D+

custom parts:
  DotStar Strip -- White (60/m): NeopixelDotStar Strip, White, 60 pixels per meter.
  Adafruit Micro USB Breakout: Simple but effective - this breakout board has a USB Micro-B connector, with all 5 pins broken out. Great for pairing with a microcontroller with USB support, or adding USB 5V power to a project. We use a micro-AB connector with through-hole shielding pads for an excellent strong connection - it won't rip off by accident! Comes with one fully assembled and tested micro B breakout PCB and a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
  USB_MICROB_PLUG: USB Micro-B Plug Comes in a variety of packages. Check out Hirose's ZX-x0 line: http://www.hirose.co.jp/cataloge_hp/e24200011.pdf
